// Logisim project librairies.circ as structural Verilog: 15 circuits, main circuit Add1bit
module Add1bit (
  input  A,
  input  B,
  input  C_in,
  output D,
  output C_out
);

  wire AND_2_out, AND_3_out, AND_out, XOR_out;

  and AND (AND_out, A, B);
  and AND_2 (AND_2_out, A, C_in);
  and AND_3 (AND_3_out, B, C_in);
  xor XOR (XOR_out, A, B);
  xor XOR_2 (D, XOR_out, C_in);
  or OR (C_out, AND_out, AND_2_out, AND_3_out);
endmodule

module Add4bits (
  input  C_in,
  input  [3:0] A,
  input  [3:0] B,
  output [3:0] D,
  output C_out
);

  wire add1bit_1_c_out, add1bit_2_c_out, add1bit_3_c_out;

  Add1bit add1bit_1 (.A(A[0]), .B(B[0]), .C_in(C_in), .D(D[0]), .C_out(add1bit_1_c_out));
  Add1bit add1bit_2 (.A(A[1]), .B(B[1]), .C_in(add1bit_1_c_out), .D(D[1]), .C_out(add1bit_2_c_out));
  Add1bit add1bit_3 (.A(A[2]), .B(B[2]), .C_in(add1bit_2_c_out), .D(D[2]), .C_out(add1bit_3_c_out));
  Add1bit add1bit_4 (.A(A[3]), .B(B[3]), .C_in(add1bit_3_c_out), .D(D[3]), .C_out(C_out));
endmodule

module binTo7seg (
  input  IN3,
  input  IN2,
  input  IN1,
  input  IN0,
  output A,
  output B,
  output C,
  output D,
  output E,
  output F,
  output G
);

  wire AND_2_out, AND_3_out, AND_4_out, AND_5_out, AND_6_out, AND_7_out, AND_8_out, AND_9_out, AND_10_out,
       AND_11_out, AND_12_out, AND_13_out, AND_14_out, AND_15_out, AND_16_out, AND_17_out, AND_18_out,
       AND_19_out, AND_20_out, AND_21_out, AND_22_out, AND_out, NOR_out, OR_2_out, OR_3_out, OR_4_out,
       OR_5_out, OR_6_out, OR_7_out, OR_8_out, OR_9_out, OR_10_out, OR_11_out, OR_12_out, OR_out, XNOR_out,
       XOR_2_out, XOR_out;

  or OR (OR_out, ~IN2, IN3);  // OR_Gate
  or OR_2 (OR_2_out, IN1, IN3);
  and AND (AND_out, ~IN0, IN1);  // AND_Gate
  and AND_2 (AND_2_out, IN0, IN2);
  xnor XNOR (XNOR_out, IN1, IN0);
  and AND_3 (AND_3_out, IN0, IN1);
  or OR_3 (OR_3_out, ~IN0, ~IN2);  // OR_Gate
  or OR_4 (OR_4_out, IN0, ~IN2);  // OR_Gate
  and AND_4 (AND_4_out, ~IN0, OR_out);  // AND_Gate
  or OR_5 (OR_5_out, ~IN2, XNOR_out);  // OR_Gate
  nor NOR (NOR_out, IN0, IN3);
  or OR_6 (OR_6_out, ~IN0, IN1, IN2);  // OR_Gate
  or OR_7 (OR_7_out, IN1, ~IN2);  // OR_Gate
  or OR_8 (OR_8_out, ~OR_2_out, AND_out);  // OR_Gate
  or OR_9 (OR_9_out, AND_2_out, IN1);
  and AND_5 (AND_5_out, IN1, IN2);
  and AND_6 (AND_6_out, IN3, ~IN2, ~IN1);  // AND_Gate
  or OR_10 (OR_10_out, IN0, ~IN3);  // OR_Gate
  xor XOR (XOR_out, IN0, IN1);
  or OR_11 (OR_11_out, AND_3_out, NOR_out);
  and AND_7 (AND_7_out, ~IN3, OR_9_out);  // AND_Gate
  and AND_8 (AND_8_out, ~IN3, OR_5_out);  // AND_Gate
  and AND_9 (AND_9_out, ~IN2, ~IN0);  // AND_Gate
  and AND_10 (AND_10_out, IN0, ~IN1, IN3);  // AND_Gate
  xor XOR_2 (XOR_2_out, IN2, IN3);
  and AND_11 (AND_11_out, ~IN1, OR_10_out);  // AND_Gate
  and AND_12 (AND_12_out, IN0, ~IN3);  // AND_Gate
  and AND_13 (AND_13_out, XOR_out, IN2);
  and AND_14 (AND_14_out, OR_11_out, ~IN2);  // AND_Gate
  and AND_15 (AND_15_out, IN3, ~IN1);  // AND_Gate
  and AND_16 (AND_16_out, OR_6_out, IN3);
  and AND_17 (AND_17_out, ~IN0, OR_7_out);  // AND_Gate
  and AND_18 (AND_18_out, OR_7_out, IN3);
  and AND_19 (AND_19_out, IN2, OR_8_out);
  or OR_12 (OR_12_out, IN0, IN1);
  and AND_20 (AND_20_out, ~IN3, IN2, ~IN1);  // AND_Gate
  and AND_21 (AND_21_out, IN1, OR_3_out);
  and AND_22 (AND_22_out, OR_4_out, IN3);
  or OR_13 (B, AND_8_out, AND_9_out, AND_10_out);
  or OR_14 (C, XOR_2_out, AND_11_out, AND_12_out);
  or OR_15 (D, AND_13_out, AND_14_out, AND_15_out);
  or OR_16 (E, AND_16_out, AND_17_out);
  or OR_17 (F, AND_18_out, AND_19_out, ~OR_12_out);  // OR_Gate
  or OR_18 (G, AND_20_out, AND_21_out, AND_22_out);
  or OR_19 (A, AND_4_out, AND_7_out, AND_5_out, AND_6_out);
endmodule

module aluSimple (
  input  Cin,
  input  [7:0] A,
  input  [7:0] B,
  input  OP,
  output V,
  output Z,
  output N,
  output [7:0] R,
  output Cout
);

  wire AND_2_out, AND_out;
  wire [7:0] XOR_out;

  assign XOR_out = B ^ {8{OP}};  // XOR_Gate XOR, 8 bits wide
  Adder adder_1 (.a(A), .b(XOR_out), .out({N, R[6:0]}), .cin(Cin), .cout(Cout));
  and AND (AND_out, ~A[7], ~XOR_out[7], N);  // AND_Gate
  and AND_2 (AND_2_out, A[7], XOR_out[7], ~N);  // AND_Gate
  or OR (V, AND_out, AND_2_out);
  and AND_3 (Z, ~R[0], ~R[1], ~R[2], ~R[3], ~R[4], ~R[5], ~R[6], ~N);  // AND_Gate

  assign R[7] = N;
endmodule

module aluComplexe8bits (
  input  [2:0] OP,
  input  [7:0] A,
  input  [7:0] B,
  output Z,
  output N,
  output C,
  output V,
  output [3:0] fanionsZNCV,
  output [7:0] R
);

  wire [7:0] alus_r, AND_out, NOT_out, OR_out;

  assign AND_out = A & B;  // AND_Gate AND, 8 bits wide
  assign OR_out = A | B;  // OR_Gate OR, 8 bits wide
  assign NOT_out = ~A;  // NOT_Gate NOT, 8 bits wide
  aluSimple alus (
    .Cin(OP[0]), .A(A), .B(B), .OP(OP[0]), .V(fanionsZNCV[0]), .Z(fanionsZNCV[3]), .N(fanionsZNCV[2]),
    .R(alus_r), .Cout(C));
  Multiplexer #(.select(3), .width(8), .enable("false")) multiplexer_1 (
    .in0(alus_r), .in1(alus_r), .in2({A[6:0], 1'b0}), .in3({1'b0, A[7:1]}), .in4({{2{A[7]}}, A[6:1]}),
    .in5(AND_out), .in6(OR_out), .in7(NOT_out), .out(R), .sel(OP));

  assign fanionsZNCV[1] = C;
  assign N = fanionsZNCV[2];
  assign V = fanionsZNCV[0];
  assign Z = fanionsZNCV[3];
endmodule

module pression (
  input  set,
  input  entree,
  input  clock,
  input  reset,
  output sortie
);

  wire flip1_q, flip2_q;

  D_Flip_Flop flip1 (.D(entree), .clk(clock), .Q(flip1_q), .preset(set), .reset(reset));  // open: Qn
  D_Flip_Flop flip2 (.D(flip1_q), .clk(clock), .Q(flip2_q), .preset(set), .reset(reset));  // open: Qn
  and AND (sortie, ~flip1_q, flip2_q);  // AND_Gate
endmodule

module interrupteur (
  input  bouton,
  input  clock,
  output sortie
);

  wire pression_1_sortie, XOR_out;

  pression pression_1 (.entree(bouton), .clock(clock), .sortie(pression_1_sortie));  // open: set, reset
  D_Flip_Flop flip3 (.D(XOR_out), .clk(clock), .Q(sortie));  // open: Qn, preset, reset
  xor XOR (XOR_out, pression_1_sortie, sortie);

  // Notes on the sheet:
  //   Interrupteur
endmodule

module seg7x4 (
  input  [3:0] IN0,
  input  [3:0] IN1,
  input  [3:0] IN2,
  input  [3:0] IN3,
  input  clk,
  output OUT0,
  output OUT1,
  output OUT2,
  output OUT3,
  output b,
  output a,
  output f,
  output g,
  output c,
  output d,
  output e
);

  wire cpt_freq_carry;
  wire [1:0] cpt_afficheur_q;
  wire [3:0] multiplexer_1_out;

  Counter #(.width(16), .max('h86a0)) cpt_freq (.clk(clk), .carry(cpt_freq_carry));  // open: clr, load, up, count, D, Q
  Counter #(.width(2), .max('h3)) cpt_afficheur (
    .count(cpt_freq_carry), .clk(clk), .Q(cpt_afficheur_q));  // open: clr, load, up, D, carry
  Decoder #(.select(2), .enable("false")) decoder_1 (
    .out0(OUT0), .out1(OUT1), .out2(OUT2), .out3(OUT3), .sel(cpt_afficheur_q));
  Multiplexer #(.select(2), .width(4), .enable("false")) multiplexer_1 (
    .in0(IN0), .in1(IN1), .in2(IN2), .in3(IN3), .out(multiplexer_1_out), .sel(cpt_afficheur_q));
  binTo7seg bin (
    .A(a), .B(b), .C(c), .D(d), .E(e), .F(f), .G(g), .IN3(multiplexer_1_out[3]), .IN2(multiplexer_1_out[2]),
    .IN1(multiplexer_1_out[1]), .IN0(multiplexer_1_out[0]));

  // Other names for the same wires on the sheet: tun_clk = clk
endmodule

module seg7x4_reg (
  input  [3:0] IN0,
  input  [3:0] IN1,
  input  [3:0] IN2,
  input  [3:0] address,
  input  enable,
  input  clock,
  input  reset,
  input  [3:0] IN3,
  output OUT0,
  output OUT1,
  output OUT2,
  output OUT3,
  output b,
  output a,
  output f,
  output g,
  output c,
  output d,
  output e
);

  wire cpt_freq_carry, decoder_1_out0, decoder_1_out1;
  wire [1:0] cpt_afficheur_q;
  wire [3:0] multiplexer_1_out, reg0_q, reg1_q, reg2_q, reg3_q;

  Counter #(.width(16), .max('h86a0)) cpt_freq (
    .clr(reset), .clk(clock), .carry(cpt_freq_carry));  // open: load, up, count, D, Q
  Decoder #(.select(4)) decoder_1 (
    .out0(decoder_1_out0), .out1(decoder_1_out1), .sel(address), .en(enable));  // open: out2, out3, out4, out5, out6, out7, out8, out9, out10, out11, out12, out13, out14, out15
  Counter #(.width(2), .max('h3)) cpt_afficheur (
    .clr(reset), .count(cpt_freq_carry), .clk(clock), .Q(cpt_afficheur_q));  // open: load, up, D, carry
  Register #(.width(4)) reg0 (.D(IN0), .en(decoder_1_out0), .clk(clock), .Q(reg0_q), .clr(reset));
  Register #(.width(4)) reg1 (.D(IN1), .en(decoder_1_out0), .clk(clock), .Q(reg1_q), .clr(reset));
  Register #(.width(4)) reg2 (.D(IN2), .en(decoder_1_out1), .clk(clock), .Q(reg2_q), .clr(reset));
  Register #(.width(4)) reg3 (.D(IN3), .en(decoder_1_out1), .clk(clock), .Q(reg3_q), .clr(reset));
  Multiplexer #(.select(2), .width(4), .enable("false")) multiplexer_1 (
    .in0(reg0_q), .in1(reg1_q), .in2(reg2_q), .in3(reg3_q), .out(multiplexer_1_out), .sel(cpt_afficheur_q));
  Decoder #(.select(2), .enable("false")) decoder_2 (
    .out0(OUT0), .out1(OUT1), .out2(OUT2), .out3(OUT3), .sel(cpt_afficheur_q));
  binTo7seg bin (
    .A(a), .B(b), .C(c), .D(d), .E(e), .F(f), .G(g), .IN3(multiplexer_1_out[3]), .IN2(multiplexer_1_out[2]),
    .IN1(multiplexer_1_out[1]), .IN0(multiplexer_1_out[0]));
endmodule

module compteur4bits (
  input  reset,
  input  load,
  input  updown,
  input  enable,
  input  clock,
  input  [3:0] data,
  input  [3:0] max,
  input  resteMax,
  output carry,
  output [3:0] current
);

  wire And_out, OR_out;
  wire [3:0] adder_1_out, multiplexer_1_out, multiplexer_2_out, multiplexer_3_out, multiplexer_4_out,
       multiplexer_5_out, multiplexer_6_out, multiplexer_7_out;

  Multiplexer #(.width(4), .enable("false")) multiplexer_1 (
    .in0(4'b1111), .in1(4'b0001), .out(multiplexer_1_out), .sel(updown));
  Multiplexer #(.width(4), .enable("false")) multiplexer_2 (
    .in0(max), .in1(4'b0000), .out(multiplexer_2_out), .sel(updown));
  Multiplexer #(.width(4), .enable("false")) multiplexer_3 (
    .in0(4'b0000), .in1(max), .out(multiplexer_3_out), .sel(updown));
  Adder #(.width(4)) adder_1 (.a(current), .b(multiplexer_1_out), .out(adder_1_out));  // open: cin, cout
  Comparator #(.width(4), .mode("unsigned")) comparator_1 (
    .a(multiplexer_3_out), .b(current), .eq(carry));  // open: gt, lt
  Multiplexer #(.width(4), .enable("false")) multiplexer_4 (
    .in0(current), .in1(adder_1_out), .out(multiplexer_4_out), .sel(enable));
  Multiplexer #(.width(4), .enable("false")) multiplexer_5 (
    .in0(data), .in1(multiplexer_2_out), .out(multiplexer_5_out), .sel(carry));
  or OR (OR_out, load, carry);
  Multiplexer #(.width(4), .enable("false")) multiplexer_6 (
    .in0(multiplexer_4_out), .in1(multiplexer_5_out), .out(multiplexer_6_out), .sel(OR_out));
  and And (And_out, carry, resteMax);
  Multiplexer #(.width(4), .enable("false")) multiplexer_7 (
    .in0(multiplexer_6_out), .in1(current), .out(multiplexer_7_out), .sel(And_out));
  Register #(.width(4)) cpt (.D(multiplexer_7_out), .en(enable), .clk(clock), .Q(current), .clr(reset));

  // Other names for the same wires on the sheet: t_carry = carry; t_clk = clock; t_curr[3:0] = current;
  //   t_data[3:0] = data; t_en = enable; t_load = load; t_max[3:0] = max; t_reste = resteMax; t_rst = reset;
  //   t_updwn = updown

  // Notes on the sheet:
  //   carry passe à 1 lorsque on arrive au max ou au min du compteur
  //   restemax indique s'il faut garder la valeur max ou min respectivement
  //   du compteur (max ou min).
  //   Ici en haut à gauche, les conditions en cascade pour
  //   incrémenter ou non de 1, puis enable ou non, ensuite
  //   les cas de load (si on a le signal ou si on arrive aux valeurs
  //   max ou min) et enfin pour savoir si on reste à la valeur finale
  //   ici en bas à gauche, on a les conditions pour load 0 
  //   ou la valeur max, selon si on incrémente ou non
endmodule

module compteur5bits (
  input  reset,
  input  load,
  input  updown,
  input  enable,
  input  clock,
  input  [4:0] data,
  input  [4:0] max,
  input  resteMax,
  output carry,
  output [4:0] current
);

  wire And_out, OR_out;
  wire [4:0] adder_1_out, multiplexer_1_out, multiplexer_2_out, multiplexer_3_out, multiplexer_4_out,
       multiplexer_5_out, multiplexer_6_out, multiplexer_7_out;

  Multiplexer #(.width(5), .enable("false")) multiplexer_1 (
    .in0({5{1'b1}}), .in1(5'b00001), .out(multiplexer_1_out), .sel(updown));
  Multiplexer #(.width(5), .enable("false")) multiplexer_2 (
    .in0(max), .in1({5{1'b0}}), .out(multiplexer_2_out), .sel(updown));
  Multiplexer #(.width(5), .enable("false")) multiplexer_3 (
    .in0({5{1'b0}}), .in1(max), .out(multiplexer_3_out), .sel(updown));
  Adder #(.width(5)) adder_1 (.a(current), .b(multiplexer_1_out), .out(adder_1_out));  // open: cin, cout
  Comparator #(.width(5), .mode("unsigned")) comparator_1 (
    .a(multiplexer_3_out), .b(current), .eq(carry));  // open: gt, lt
  Multiplexer #(.width(5), .enable("false")) multiplexer_4 (
    .in0(current), .in1(adder_1_out), .out(multiplexer_4_out), .sel(enable));
  Multiplexer #(.width(5), .enable("false")) multiplexer_5 (
    .in0(data), .in1(multiplexer_2_out), .out(multiplexer_5_out), .sel(carry));
  or OR (OR_out, load, carry);
  Multiplexer #(.width(5), .enable("false")) multiplexer_6 (
    .in0(multiplexer_4_out), .in1(multiplexer_5_out), .out(multiplexer_6_out), .sel(OR_out));
  and And (And_out, carry, resteMax);
  Multiplexer #(.width(5), .enable("false")) multiplexer_7 (
    .in0(multiplexer_6_out), .in1(current), .out(multiplexer_7_out), .sel(And_out));
  Register #(.width(5)) cpt (.D(multiplexer_7_out), .en(enable), .clk(clock), .Q(current), .clr(reset));

  // Other names for the same wires on the sheet: t_carry = carry; t_clk = clock; t_curr[4:0] = current;
  //   t_data[4:0] = data; t_en = enable; t_load = load; t_max[4:0] = max; t_reste = resteMax; t_rst = reset;
  //   t_updwn = updown

  // Notes on the sheet:
  //   carry passe à 1 lorsque on arrive au max ou au min du compteur
  //   restemax indique s'il faut garder la valeur max ou min respectivement
  //   du compteur (max ou min).
  //   Ici en haut à gauche, les conditions en cascade pour
  //   incrémenter ou non de 1, puis enable ou non, ensuite
  //   les cas de load (si on a le signal ou si on arrive aux valeurs
  //   max ou min) et enfin pour savoir si on reste à la valeur finale
  //   ici en bas à gauche, on a les conditions pour load 0 
  //   ou la valeur max, selon si on incrémente ou non
endmodule

module compteur6bits (
  input  reset,
  input  load,
  input  updown,
  input  enable,
  input  clock,
  input  [5:0] data,
  input  [5:0] max,
  input  resteMax,
  output carry,
  output [5:0] current
);

  wire And_out, OR_out;
  wire [5:0] adder_1_out, multiplexer_1_out, multiplexer_2_out, multiplexer_3_out, multiplexer_4_out,
       multiplexer_5_out, multiplexer_6_out, multiplexer_7_out;

  Multiplexer #(.width(6), .enable("false")) multiplexer_1 (
    .in0({6{1'b1}}), .in1(6'b000001), .out(multiplexer_1_out), .sel(updown));
  Multiplexer #(.width(6), .enable("false")) multiplexer_2 (
    .in0(max), .in1({6{1'b0}}), .out(multiplexer_2_out), .sel(updown));
  Multiplexer #(.width(6), .enable("false")) multiplexer_3 (
    .in0({6{1'b0}}), .in1(max), .out(multiplexer_3_out), .sel(updown));
  Adder #(.width(6)) adder_1 (.a(current), .b(multiplexer_1_out), .out(adder_1_out));  // open: cin, cout
  Comparator #(.width(6), .mode("unsigned")) comparator_1 (
    .a(multiplexer_3_out), .b(current), .eq(carry));  // open: gt, lt
  Multiplexer #(.width(6), .enable("false")) multiplexer_4 (
    .in0(current), .in1(adder_1_out), .out(multiplexer_4_out), .sel(enable));
  Multiplexer #(.width(6), .enable("false")) multiplexer_5 (
    .in0(data), .in1(multiplexer_2_out), .out(multiplexer_5_out), .sel(carry));
  or OR (OR_out, load, carry);
  Multiplexer #(.width(6), .enable("false")) multiplexer_6 (
    .in0(multiplexer_4_out), .in1(multiplexer_5_out), .out(multiplexer_6_out), .sel(OR_out));
  and And (And_out, carry, resteMax);
  Multiplexer #(.width(6), .enable("false")) multiplexer_7 (
    .in0(multiplexer_6_out), .in1(current), .out(multiplexer_7_out), .sel(And_out));
  Register #(.width(6)) cpt (.D(multiplexer_7_out), .en(enable), .clk(clock), .Q(current), .clr(reset));

  // Other names for the same wires on the sheet: t_carry = carry; t_clk = clock; t_curr[5:0] = current;
  //   t_data[5:0] = data; t_en = enable; t_load = load; t_max[5:0] = max; t_reste = resteMax; t_rst = reset;
  //   t_updwn = updown

  // Notes on the sheet:
  //   carry passe à 1 lorsque on arrive au max ou au min du compteur
  //   restemax indique s'il faut garder la valeur max ou min respectivement
  //   du compteur (max ou min).
  //   Ici en haut à gauche, les conditions en cascade pour
  //   incrémenter ou non de 1, puis enable ou non, ensuite
  //   les cas de load (si on a le signal ou si on arrive aux valeurs
  //   max ou min) et enfin pour savoir si on reste à la valeur finale
  //   ici en bas à gauche, on a les conditions pour load 0 
  //   ou la valeur max, selon si on incrémente ou non
endmodule

module compteur8bits (
  input  reset,
  input  load,
  input  updown,
  input  enable,
  input  clock,
  input  [7:0] data,
  input  [7:0] max,
  input  resteMax,
  output carry,
  output [7:0] current
);

  wire And_out, OR_out;
  wire [7:0] adder_1_out, multiplexer_1_out, multiplexer_2_out, multiplexer_3_out, multiplexer_4_out,
       multiplexer_5_out, multiplexer_6_out, multiplexer_7_out;

  Multiplexer #(.width(8), .enable("false")) multiplexer_1 (
    .in0({8{1'b1}}), .in1(8'h1), .out(multiplexer_1_out), .sel(updown));
  Multiplexer #(.width(8), .enable("false")) multiplexer_2 (
    .in0(max), .in1({8{1'b0}}), .out(multiplexer_2_out), .sel(updown));
  Multiplexer #(.width(8), .enable("false")) multiplexer_3 (
    .in0({8{1'b0}}), .in1(max), .out(multiplexer_3_out), .sel(updown));
  Adder adder_1 (.a(current), .b(multiplexer_1_out), .out(adder_1_out));  // open: cin, cout
  Comparator #(.mode("unsigned")) comparator_1 (.a(multiplexer_3_out), .b(current), .eq(carry));  // open: gt, lt
  Multiplexer #(.width(8), .enable("false")) multiplexer_4 (
    .in0(current), .in1(adder_1_out), .out(multiplexer_4_out), .sel(enable));
  Multiplexer #(.width(8), .enable("false")) multiplexer_5 (
    .in0(data), .in1(multiplexer_2_out), .out(multiplexer_5_out), .sel(carry));
  or OR (OR_out, load, carry);
  Multiplexer #(.width(8), .enable("false")) multiplexer_6 (
    .in0(multiplexer_4_out), .in1(multiplexer_5_out), .out(multiplexer_6_out), .sel(OR_out));
  and And (And_out, carry, resteMax);
  Multiplexer #(.width(8), .enable("false")) multiplexer_7 (
    .in0(multiplexer_6_out), .in1(current), .out(multiplexer_7_out), .sel(And_out));
  Register cpt (.D(multiplexer_7_out), .en(enable), .clk(clock), .Q(current), .clr(reset));

  // Other names for the same wires on the sheet: t_carry = carry; t_clk = clock; t_curr[7:0] = current;
  //   t_data[7:0] = data; t_en = enable; t_load = load; t_max[7:0] = max; t_reste = resteMax; t_rst = reset;
  //   t_updwn = updown

  // Notes on the sheet:
  //   carry passe à 1 lorsque on arrive au max ou au min du compteur
  //   restemax indique s'il faut garder la valeur max ou min respectivement
  //   du compteur (max ou min).
  //   Ici en haut à gauche, les conditions en cascade pour
  //   incrémenter ou non de 1, puis enable ou non, ensuite
  //   les cas de load (si on a le signal ou si on arrive aux valeurs
  //   max ou min) et enfin pour savoir si on reste à la valeur finale
  //   ici en bas à gauche, on a les conditions pour load 0 
  //   ou la valeur max, selon si on incrémente ou non
endmodule

module compteur10bits (
  input  reset,
  input  load,
  input  updown,
  input  enable,
  input  clock,
  input  [9:0] data,
  input  [9:0] max,
  input  resteMax,
  output carry,
  output [9:0] current
);

  wire And_out, OR_out;
  wire [9:0] adder_1_out, multiplexer_1_out, multiplexer_2_out, multiplexer_3_out, multiplexer_4_out,
       multiplexer_5_out, multiplexer_6_out, multiplexer_7_out;

  Multiplexer #(.width(10), .enable("false")) multiplexer_1 (
    .in0({10{1'b1}}), .in1(10'h1), .out(multiplexer_1_out), .sel(updown));
  Multiplexer #(.width(10), .enable("false")) multiplexer_2 (
    .in0(max), .in1({10{1'b0}}), .out(multiplexer_2_out), .sel(updown));
  Multiplexer #(.width(10), .enable("false")) multiplexer_3 (
    .in0({10{1'b0}}), .in1(max), .out(multiplexer_3_out), .sel(updown));
  Adder #(.width(10)) adder_1 (.a(current), .b(multiplexer_1_out), .out(adder_1_out));  // open: cin, cout
  Comparator #(.width(10), .mode("unsigned")) comparator_1 (
    .a(multiplexer_3_out), .b(current), .eq(carry));  // open: gt, lt
  Multiplexer #(.width(10), .enable("false")) multiplexer_4 (
    .in0(current), .in1(adder_1_out), .out(multiplexer_4_out), .sel(enable));
  Multiplexer #(.width(10), .enable("false")) multiplexer_5 (
    .in0(data), .in1(multiplexer_2_out), .out(multiplexer_5_out), .sel(carry));
  or OR (OR_out, load, carry);
  Multiplexer #(.width(10), .enable("false")) multiplexer_6 (
    .in0(multiplexer_4_out), .in1(multiplexer_5_out), .out(multiplexer_6_out), .sel(OR_out));
  and And (And_out, carry, resteMax);
  Multiplexer #(.width(10), .enable("false")) multiplexer_7 (
    .in0(multiplexer_6_out), .in1(current), .out(multiplexer_7_out), .sel(And_out));
  Register #(.width(10)) cpt (.D(multiplexer_7_out), .en(enable), .clk(clock), .Q(current), .clr(reset));

  // Other names for the same wires on the sheet: t_carry = carry; t_clk = clock; t_curr[9:0] = current;
  //   t_data[9:0] = data; t_en = enable; t_load = load; t_max[9:0] = max; t_reste = resteMax; t_rst = reset;
  //   t_updwn = updown

  // Notes on the sheet:
  //   carry passe à 1 lorsque on arrive au max ou au min du compteur
  //   restemax indique s'il faut garder la valeur max ou min respectivement
  //   du compteur (max ou min).
  //   Ici en haut à gauche, les conditions en cascade pour
  //   incrémenter ou non de 1, puis enable ou non, ensuite
  //   les cas de load (si on a le signal ou si on arrive aux valeurs
  //   max ou min) et enfin pour savoir si on reste à la valeur finale
  //   ici en bas à gauche, on a les conditions pour load 0 
  //   ou la valeur max, selon si on incrémente ou non
endmodule

module cadenas4digits (
  input  a,
  input  [2:0] etatFinal,
  input  b,
  input  [1:0] lettre,
  input  [2:0] etatPresent,
  input  d,
  input  c,
  input  clk,
  input  reset,
  output led
);

  wire pressA_sortie, pressB_sortie, pressC_sortie, pressD_sortie, pressReset_sortie, priority_encoder_1_gs;

  pression pressA (.entree(a), .clock(clk), .sortie(pressA_sortie));  // open: set, reset
  pression pressB (.entree(b), .clock(clk), .sortie(pressB_sortie));  // open: set, reset
  pression pressD (.entree(d), .clock(clk), .sortie(pressD_sortie));  // open: set, reset
  pression pressC (.entree(c), .clock(clk), .sortie(pressC_sortie));  // open: set, reset
  Priority_Encoder #(.select(2)) priority_encoder_1 (
    .in0(pressA_sortie), .in1(pressB_sortie), .in2(pressD_sortie), .in3(pressC_sortie), .out(lettre),
    .gs(priority_encoder_1_gs));  // open: en_out, en_in
  Register #(.width(3)) registre (
    .D(etatFinal), .en(priority_encoder_1_gs), .clk(clk), .Q(etatPresent), .clr(pressReset_sortie));
  pression pressReset (.entree(reset), .clock(clk), .sortie(pressReset_sortie));  // open: set, reset
  Comparator #(.width(3), .mode("unsigned")) comparator_1 (.a(etatPresent), .b(3'b100), .eq(led));  // open: gt, lt

  // Other names for the same wires on the sheet: t_lettre[1:0] = lettre
endmodule
