// Logisim project schema_rapport.circ as structural Verilog
module main_wifi (
);

  wire basys_commande_out, basys_moteurs_out, basys_moteurs_out1, capteur_droit_out, capteur_gauche_out,
       pont_H_out, pont_H_out_2, tlc0_out, tlc0_out_2, tlc0_out_3, tlc1_out, tlc1_out_2, wifly1_out;

  infra capteur_gauche (.out(capteur_gauche_out));
  infra capteur_droit (.out(capteur_droit_out));
  tlc tlc0 (.in(capteur_gauche_out), .out(tlc0_out), .out_2(tlc0_out_2), .out_3(tlc0_out_3));
  tlc tlc1 (.in(capteur_droit_out), .out(tlc1_out), .out_2(tlc1_out_2), .out_3(tlc0_out_3));
  basys_commande basys_commande (
    .out(basys_commande_out), .in(tlc0_out), .in1(tlc0_out_2), .in_2(tlc0_out_3), .in1_2(tlc1_out),
    .in1_3(tlc1_out_2));
  wifly wifly0 (.in(basys_commande_out));  // open: out
  air air_1 ();
  air air_2 ();
  wifly wifly1 (.out(wifly1_out));  // open: in
  basys_moteurs basys_moteurs (.in(wifly1_out), .out(basys_moteurs_out), .out1(basys_moteurs_out1));
  pontH pont_H (.in(basys_moteurs_out), .out(pont_H_out), .in_2(basys_moteurs_out1), .out_2(pont_H_out_2));
  moteur moteur_gauche (.in(pont_H_out));
  moteur moteur_droit (.in(pont_H_out_2));

  // Notes on the sheet:
  //   SPI
  //   SPI
  //   Uart
  //   Wifi
  //   Uart
endmodule

module main_fil (
);

  wire basys_commande_out, basys_moteurs_out, basys_moteurs_out1, capteur_droit_out, capteur_gauche_out,
       pont_H_out, pont_H_out_2, tlc0_out, tlc0_out_2, tlc0_out_3, tlc1_out, tlc1_out_2;

  infra capteur_gauche (.out(capteur_gauche_out));
  infra capteur_droit (.out(capteur_droit_out));
  tlc tlc0 (.in(capteur_gauche_out), .out(tlc0_out), .out_2(tlc0_out_2), .out_3(tlc0_out_3));
  tlc tlc1 (.in(capteur_droit_out), .out(tlc1_out), .out_2(tlc1_out_2), .out_3(tlc0_out_3));
  basys_commande basys_commande (
    .out(basys_commande_out), .in(tlc0_out), .in1(tlc0_out_2), .in_2(tlc0_out_3), .in1_2(tlc1_out),
    .in1_3(tlc1_out_2));
  basys_moteurs basys_moteurs (.in(basys_commande_out), .out(basys_moteurs_out), .out1(basys_moteurs_out1));
  pontH pont_H (.in(basys_moteurs_out), .out(pont_H_out), .in_2(basys_moteurs_out1), .out_2(pont_H_out_2));
  moteur moteur_gauche (.in(pont_H_out));
  moteur moteur_droit (.in(pont_H_out_2));

  // Notes on the sheet:
  //   SPI
  //   SPI
  //   Uart
endmodule

module basys_commande (
  input  in,
  input  in1,
  input  in_2,
  input  in1_2,
  input  in1_3,
  output out
);


  assign out = 1'b0;
endmodule

module basys_moteurs (
  input  in,
  output out,
  output out1
);


  assign out = 1'b0;
  assign out1 = 1'b0;
endmodule

module infra (
  output out
);


  assign out = 1'b0;
endmodule

module tlc (
  input  in,
  output out,
  output out_2,
  output out_3
);


  assign out = 1'b0;
  assign out_2 = 1'b0;
  assign out_3 = 1'b0;
endmodule

module pontH (
  input  in,
  input  in_2,
  output out,
  output out_2
);


  assign out = 1'b0;
  assign out_2 = 1'b0;
endmodule

module moteur (
  input  in
);
endmodule

module wifly (
  input  in,
  output out
);


  assign out = 1'b0;
endmodule
