// Logisim project system_moteurs.circ as structural Verilog: 8 circuits, main circuit reg_bank
module rom (
  input  [7:0] prog_counter,
  output [15:0] instruction
);

  wire [15:0] mux0, mux1, mux2, mux3, undriven, undriven_2, undriven_3, undriven_4, undriven_5, undriven_6,
       undriven_7, undriven_8, undriven_9, undriven_10, undriven_11, undriven_12, undriven_13, undriven_14,
       undriven_15, undriven_16, undriven_17, undriven_18, undriven_19, undriven_20, undriven_21,
       undriven_22, undriven_23, undriven_24, undriven_25, undriven_26, undriven_27, undriven_28,
       undriven_29, undriven_30, undriven_31, undriven_32, undriven_33, undriven_34, undriven_35,
       undriven_36, undriven_37, undriven_38, undriven_39, undriven_40, undriven_41, undriven_42,
       undriven_43, undriven_44, undriven_45, undriven_46, undriven_47, undriven_48, undriven_49,
       undriven_50, undriven_51, undriven_52, undriven_53, undriven_54, undriven_55, undriven_56,
       undriven_57, undriven_58, undriven_59, undriven_60, undriven_61, undriven_62, undriven_63,
       undriven_64, undriven_65, undriven_66, undriven_67, undriven_68, undriven_69, undriven_70,
       undriven_71, undriven_72, undriven_73, undriven_74, undriven_75, undriven_76, undriven_77,
       undriven_78, undriven_79, undriven_80, undriven_81, undriven_82, undriven_83, undriven_84,
       undriven_85, undriven_86, undriven_87, undriven_88, undriven_89, undriven_90, undriven_91,
       undriven_92, undriven_93, undriven_94, undriven_95, undriven_96, undriven_97, undriven_98,
       undriven_99, undriven_100, undriven_101, undriven_102;

  Multiplexer #(.select(5), .width(16)) multiplexer_1 (
    .in0(16'h8010), .in1(16'hc601), .in2(16'h1a18), .in3(16'ha8fe), .in4(16'hc600), .in5(16'h8230),
    .in6(16'h1a58), .in7(16'ha805), .in8(16'h8240), .in9(16'h1a58), .in10(16'ha807), .in11(16'hbff6),
    .in12(16'hc601), .in13(16'h1a18), .in14(16'ha8fe), .in15(16'hcc00), .in16(16'hbff1), .in17(16'hc601),
    .in18(16'h1a18), .in19(16'ha8fe), .in20(16'hce00), .in21(16'hdc21), .in22(16'hde31), .in23(16'hdc40),
    .in24(16'hde41), .in25(16'hbfe8), .in26(undriven), .in27(undriven_20), .in28(undriven_2),
    .in29(undriven_21), .in30(undriven_3), .in31(undriven_22), .out(mux0), .sel(prog_counter[4:0]));  // open: en
  Multiplexer #(.select(5), .width(16)) multiplexer_2 (
    .in0(undriven_4), .in1(undriven_23), .in2(undriven_5), .in3(undriven_24), .in4(undriven_6),
    .in5(undriven_25), .in6(undriven_7), .in7(undriven_26), .in8(undriven_8), .in9(undriven_27),
    .in10(undriven_9), .in11(undriven_28), .in12(undriven_10), .in13(undriven_29), .in14(undriven_11),
    .in15(undriven_30), .in16(undriven_12), .in17(undriven_31), .in18(undriven_13), .in19(undriven_32),
    .in20(undriven_14), .in21(undriven_33), .in22(undriven_15), .in23(undriven_34), .in24(undriven_16),
    .in25(undriven_35), .in26(undriven_17), .in27(undriven_36), .in28(undriven_18), .in29(undriven_37),
    .in30(undriven_19), .in31(undriven_38), .out(mux1), .sel(prog_counter[4:0]));  // open: en
  Multiplexer #(.select(5), .width(16)) multiplexer_3 (
    .in0(undriven_39), .in1(undriven_71), .in2(undriven_40), .in3(undriven_72), .in4(undriven_41),
    .in5(undriven_73), .in6(undriven_42), .in7(undriven_74), .in8(undriven_43), .in9(undriven_75),
    .in10(undriven_44), .in11(undriven_76), .in12(undriven_45), .in13(undriven_77), .in14(undriven_46),
    .in15(undriven_78), .in16(undriven_47), .in17(undriven_79), .in18(undriven_48), .in19(undriven_80),
    .in20(undriven_49), .in21(undriven_81), .in22(undriven_50), .in23(undriven_82), .in24(undriven_51),
    .in25(undriven_83), .in26(undriven_52), .in27(undriven_84), .in28(undriven_53), .in29(undriven_85),
    .in30(undriven_54), .in31(undriven_86), .out(mux2), .sel(prog_counter[4:0]));  // open: en
  Multiplexer #(.select(5), .width(16)) multiplexer_4 (
    .in0(undriven_55), .in1(undriven_87), .in2(undriven_56), .in3(undriven_88), .in4(undriven_57),
    .in5(undriven_89), .in6(undriven_58), .in7(undriven_90), .in8(undriven_59), .in9(undriven_91),
    .in10(undriven_60), .in11(undriven_92), .in12(undriven_61), .in13(undriven_93), .in14(undriven_62),
    .in15(undriven_94), .in16(undriven_63), .in17(undriven_95), .in18(undriven_64), .in19(undriven_96),
    .in20(undriven_65), .in21(undriven_97), .in22(undriven_66), .in23(undriven_98), .in24(undriven_67),
    .in25(undriven_99), .in26(undriven_68), .in27(undriven_100), .in28(undriven_69), .in29(undriven_101),
    .in30(undriven_70), .in31(undriven_102), .out(mux3), .sel(prog_counter[4:0]));  // open: en
  Multiplexer #(.select(2), .width(16)) multiplexer_5 (
    .in0(mux0), .in1(mux1), .in2(mux2), .in3(mux3), .out(instruction), .sel(prog_counter[7:6]));  // open: en
  // Probe on instruction

  // Other names for the same wires on the sheet: sel[1:0] = prog_counter[7:6]
endmodule

module reg_bank (
  input  [7:0] data_write,
  input  wr_enable,
  input  [2:0] addr_write,
  input  [2:0] addr_read_A,
  input  [2:0] addr_read_B,
  input  clock,
  input  reset,
  output [7:0] data_read_A,
  output [7:0] data_read_B
);

  wire dec0, dec1, dec2, dec4, dec5, dec6, dec7, tdec3;
  wire [7:0] reg0, reg1, reg2, reg3, reg4, reg5, reg6, reg7;

  Decoder #(.select(3)) decoder_1 (
    .out0(dec0), .out1(dec1), .out2(dec2), .out3(tdec3), .out4(dec4), .out5(dec5), .out6(dec6), .out7(dec7),
    .sel(addr_write), .en(wr_enable));
  Register u_reg0 (.D(data_write), .en(dec0), .clk(clock), .Q(reg0), .clr(reset));
  Register u_reg1 (.D(data_write), .en(dec1), .clk(clock), .Q(reg1), .clr(reset));
  Register u_reg2 (.D(data_write), .en(dec2), .clk(clock), .Q(reg2), .clr(reset));
  Register u_reg3 (.D(data_write), .en(tdec3), .clk(clock), .Q(reg3), .clr(reset));
  // Probe on reg0
  // Probe on reg1
  // Probe on reg2
  // Probe on reg3
  Register u_reg4 (.D(data_write), .en(dec4), .clk(clock), .Q(reg4), .clr(reset));
  Register u_reg5 (.D(data_write), .en(dec5), .clk(clock), .Q(reg5), .clr(reset));
  Register u_reg6 (.D(data_write), .en(dec6), .clk(clock), .Q(reg6), .clr(reset));
  Register u_reg7 (.D(data_write), .en(dec7), .clk(clock), .Q(reg7), .clr(reset));
  // Probe on reg4
  // Probe on reg5
  // Probe on reg6
  // Probe on reg7
  Multiplexer #(.select(3), .width(8), .enable("false")) multiplexer_1 (
    .in0(reg0), .in1(reg1), .in2(reg2), .in3(reg3), .in4(reg4), .in5(reg5), .in6(reg6), .in7(reg7),
    .out(data_read_A), .sel(addr_read_A));
  Multiplexer #(.select(3), .width(8), .enable("false")) multiplexer_2 (
    .in0(reg0), .in1(reg1), .in2(reg2), .in3(reg3), .in4(reg4), .in5(reg5), .in6(reg6), .in7(reg7),
    .out(data_read_B), .sel(addr_read_B));
  // Probe on data_read_A
  // Probe on data_read_B
endmodule

module control_unit (
  input  [15:0] instruction,
  input  [3:0] fanions,
  input  [7:0] prog_counter,
  input  [7:0] result,
  input  [7:0] data_periph_read,
  output [7:0] data_write,
  output [7:0] address_periph,
  output perip_w,
  output perip_r,
  output we_fanions,
  output load,
  output [2:0] op_alu,
  output [2:0] addr_write,
  output wr_enable,
  output [2:0] addr_read_A,
  output [2:0] addr_read_B,
  output [7:0] saut
);

  wire AND_2_out, decoder_1_out8, decoder_1_out10, decoder_1_out11, OR_2_out, OR_out;
  wire [2:0] multiplexer_2_out;
  wire [3:0] AND_out;
  wire [7:0] multiplexer_5_out;

  // Probe on instruction
  Multiplexer #(.width(3), .enable("false")) multiplexer_1 (
    .in0(instruction[5:3]), .in1(3'b000), .out(addr_read_B), .sel(instruction[15]));
  Multiplexer #(.width(3), .enable("false")) multiplexer_2 (
    .in0(instruction[8:6]), .in1(3'b000), .out(multiplexer_2_out), .sel(instruction[15]));
  Decoder #(.select(4), .enable("false")) decoder_1 (
    .out8(decoder_1_out8), .out10(decoder_1_out10), .out11(decoder_1_out11), .out12(perip_r),
    .out13(perip_w), .sel(instruction[15:12]));  // open: out0, out1, out2, out3, out4, out5, out6, out7, out9, out14, out15
  not not_1 (we_fanions, instruction[15]);
  Multiplexer #(.width(3), .enable("false")) multiplexer_3 (
    .in0(instruction[14:12]), .in1(3'b000), .out(op_alu), .sel(instruction[15]));
  Multiplexer #(.width(3), .enable("false")) multiplexer_4 (
    .in0(multiplexer_2_out), .in1(instruction[11:9]), .out(addr_read_A), .sel(perip_w));
  assign AND_out = fanions & instruction[11:8];  // AND_Gate AND, 4 bits wide
  Multiplexer #(.width(8), .enable("false")) multiplexer_5 (
    .in0(result), .in1(instruction[7:0]), .out(multiplexer_5_out), .sel(decoder_1_out8));
  or OR (OR_out, AND_out[3], AND_out[2], AND_out[1], AND_out[0]);
  Multiplexer #(.width(8), .enable("false")) multiplexer_6 (
    .in0(multiplexer_5_out), .in1(data_periph_read), .out(data_write), .sel(perip_r));
  and AND_2 (AND_2_out, decoder_1_out10, OR_out);
  or OR_2 (OR_2_out, decoder_1_out10, perip_w, decoder_1_out11);
  Adder adder_1 (.a(prog_counter), .b(instruction[7:0]), .out(saut));  // open: cin, cout
  or OR_3 (load, decoder_1_out11, AND_2_out);
  not not_2 (wr_enable, OR_2_out);

  assign addr_write = instruction[11:9];
  assign address_periph = instruction[7:0];

  // Other names for the same wires on the sheet: t_8bits[7:0] = instruction[7:0]; condition[3:0] = instruction[11:8];
  //   data_periph_r[7:0] = data_periph_read

  // Notes on the sheet:
  //   écriture
  //   lecture
  //   Ici, gestion des conditions
  //   saut inconditionnel
  //   charger une constante
  //   saut conditionnel
  //   Calcul du saut (conditionnel ou inconditionnel)
endmodule

module cpu (
  input  clock,
  input  reset,
  input  [7:0] data_in,
  output read,
  output [7:0] address,
  output wr,
  output [7:0] data_out
);

  wire cu_we_fanions, cu_wr_enable, load;
  wire [2:0] cu_addr_read_a, cu_addr_read_b, cu_addr_write, cu_op_alu;
  wire [3:0] alu_fanionszncv, reg_fanions_q;
  wire [7:0] alu_r, cpt_instr_q, cu_data_write, ram_data_read_b, saut;
  wire [15:0] instr_instruction;

  Counter cpt_instr (.clr(reset), .load(load), .clk(clock), .D(saut), .Q(cpt_instr_q));  // open: up, count, carry
  // Probe on cpt_instr_q
  rom instr (.instruction(instr_instruction), .prog_counter(cpt_instr_q));
  // Probe on instr_instruction
  control_unit cu (
    .op_alu(cu_op_alu), .addr_write(cu_addr_write), .addr_read_A(cu_addr_read_a),
    .addr_read_B(cu_addr_read_b), .wr_enable(cu_wr_enable), .data_write(cu_data_write), .result(alu_r),
    .load(load), .perip_w(wr), .perip_r(read), .data_periph_read(data_in), .saut(saut),
    .instruction(instr_instruction), .prog_counter(cpt_instr_q), .fanions(reg_fanions_q),
    .address_periph(address), .we_fanions(cu_we_fanions));
  reg_bank ram (
    .data_write(cu_data_write), .wr_enable(cu_wr_enable), .addr_write(cu_addr_write),
    .addr_read_A(cu_addr_read_a), .addr_read_B(cu_addr_read_b), .clock(clock), .reset(reset),
    .data_read_A(data_out), .data_read_B(ram_data_read_b));
  aluComplexe8bits alu (
    .A(data_out), .B(ram_data_read_b), .R(alu_r), .OP(cu_op_alu), .fanionsZNCV(alu_fanionszncv));  // open: V, Z, N, C
  // Probe on alu_r
  Register #(.width(4)) reg_fanions (
    .D(alu_fanionszncv), .en(cu_we_fanions), .clk(clock), .Q(reg_fanions_q), .clr(reset));
endmodule

module spi_tlc (
  input  miso0,
  input  miso1,
  input  [3:0] address,
  input  clock,
  input  reset,
  output sclk,
  output cs0,
  output cs1,
  output [7:0] data_out
);

  wire AND_2_out, AND_out, comparator_2_eq, comparator_2_gt, comparator_2_lt, comparator_3_eq,
       comparator_3_gt, comparator_3_lt, counter_1_carry, miso0_t, miso1_t, multiplexer_1_out, OR_2_out,
       OR_out, sclk_t;
  wire [4:0] counter_2_q;
  wire [5:0] counter_1_q;
  wire [7:0] reg0_q, reg1_q, s_reg0_p5, s_reg1_p10;

  Counter #(.width(6), .max('h31)) counter_1 (
    .clr(reset), .clk(clock), .carry(counter_1_carry), .Q(counter_1_q));  // open: load, up, count, D
  Comparator #(.width(6), .mode("unsigned")) comparator_1 (
    .a(counter_1_q), .b(6'b011000), .gt(sclk_t));  // open: eq, lt
  Counter #(.width(5), .max('h1b)) counter_2 (
    .clr(reset), .count(counter_1_carry), .clk(clock), .Q(counter_2_q));  // open: load, up, D, carry
  and AND (AND_out, counter_1_carry, sclk_t, comparator_2_lt);
  // Shift_Register s_reg0: pin names not known; wires that end beside it: reset, AND_out, clock, miso0_t, s_reg0_p5[0], s_reg0_p5[1], s_reg0_p5[2]
  // Shift_Register s_reg1: pin names not known; wires that end beside it: reset, AND_out, clock, miso1_t, s_reg0_p5[3], s_reg0_p5[4], s_reg0_p5[5], s_reg0_p5[6], s_reg0_p5[7], s_reg1_p10[0], s_reg1_p10[1], s_reg1_p10[2], s_reg1_p10[3], s_reg1_p10[4], s_reg1_p10[5], s_reg1_p10[6], s_reg1_p10[7]
  // Probe on counter_2_q
  Comparator #(.width(5), .mode("unsigned")) comparator_2 (
    .a(counter_2_q), .b(5'b01000), .gt(comparator_2_gt), .eq(comparator_2_eq), .lt(comparator_2_lt));
  // Probe on 5'b11001
  Comparator #(.width(5), .mode("unsigned")) comparator_3 (
    .a(counter_2_q), .b(5'b11001), .gt(comparator_3_gt), .eq(comparator_3_eq), .lt(comparator_3_lt));
  and AND_2 (AND_2_out, comparator_3_lt, comparator_2_gt);
  or OR (OR_out, comparator_3_gt, comparator_3_eq);
  or OR_2 (OR_2_out, AND_2_out, comparator_2_eq);
  Register reg0 (.D(s_reg0_p5), .en(comparator_2_eq), .clk(clock), .Q(reg0_q), .clr(reset));
  Register reg1 (.D(s_reg1_p10), .en(comparator_2_eq), .clk(clock), .Q(reg1_q), .clr(reset));
  not not_1 (miso0_t, miso0);
  not not_2 (miso1_t, miso1);
  not not_3 (sclk, multiplexer_1_out);
  Multiplexer #(.enable("false")) multiplexer_1 (.in0(sclk_t), .in1(1'b0), .out(multiplexer_1_out), .sel(OR_out));
  not not_4 (cs0, OR_2_out);
  Multiplexer #(.width(8), .enable("false")) multiplexer_2 (
    .in0(reg0_q), .in1(reg1_q), .out(data_out), .sel(address[0]));

  assign cs1 = cs0;

  // Notes on the sheet:
  //   sclk à 1 MHz
  //   Ce compteur compte le cycle complet sur 27 coups : 8 coups pour les 8 bits, 17 coups pour chip select, 2 coups pour le temps d'attente
  //   On désactive la sclk 2 coups de clock pour respecter les 
  //   1.4 micro secondes après désactivation du chip select
endmodule

module pwm (
  input  [3:0] address,
  input  enable,
  input  [7:0] data_in,
  input  clock,
  input  reset,
  output cs,
  output out0,
  output out1
);

  wire comparator_1_lt, counter_1_carry, multiplexer_1_out, multiplexer_2_out, reg1_q;
  wire [7:0] counter_2_q, reg0_q, undriven;

  Counter #(.width(9), .max('h1f4)) counter_1 (
    .clr(reset), .clk(clock), .carry(counter_1_carry));  // open: load, up, count, D, Q
  Counter counter_2 (
    .clr(reset), .count(counter_1_carry), .clk(clock), .D(undriven), .Q(counter_2_q));  // open: load, up, carry
  Register reg0 (.D(data_in), .en(enable), .clk(clock), .Q(reg0_q), .clr(reset));
  // Probe on counter_2_q
  // Probe on reg0_q
  Register #(.width(1)) reg1 (.D(address[0]), .en(enable), .clk(clock), .Q(reg1_q), .clr(reset));
  Comparator #(.mode("unsigned")) comparator_1 (.a(counter_2_q), .b(reg0_q), .lt(comparator_1_lt));  // open: gt, eq
  Multiplexer #(.enable("false")) multiplexer_1 (
    .in0(comparator_1_lt), .in1(1'b0), .out(multiplexer_1_out), .sel(reg1_q));
  Multiplexer #(.enable("false")) multiplexer_2 (
    .in0(1'b0), .in1(comparator_1_lt), .out(multiplexer_2_out), .sel(reg1_q));
  not not_1 (out0, multiplexer_1_out);
  not not_2 (out1, multiplexer_2_out);

  assign cs = 1'b0;

  // Notes on the sheet:
  //   clock system
  //   Deux sorties pour le sens de rotation des moteurs, ne peut pas y avoir de conflit
endmodule

module uart (
  input  wr,
  input  [7:0] data_in,
  input  [3:0] address,
  input  clock,
  input  reset,
  input  Rx,
  output [7:0] data_out,
  output Tx
);

  wire AND_2_out, AND_3_out, AND_4_out, AND_5_out, AND_6_out, AND_7_out, AND_9_out, AND_out, clk_rx,
       d_ff_1_q, div_clk, inter_tram, multiplexer_1_out, multiplexer_2_out, multiplexer_3_out, not_1_out,
       not_2_out, not_3_out, not_4_out, not_5_out, OR_2_out, OR_3_out, OR_4_out, OR_5_out, receive_done,
       reg_tx1_q, reg_tx_2_q, reg_tx_3_q, rx_finish, Rx_t, s_rg_rx_p1, s_rg_tx_p16, s_rg_tx_p17, s_rg_tx_p18,
       s_rg_tx_p19, s_rg_tx_p20, s_rg_tx_p21, s_rg_tx_p22, s_rg_tx_p23, s_rg_tx_p24, s_rg_tx_p25, start,
       temp_ok, tx_finish;
  wire [3:0] counter_3_q;
  wire [7:0] data_out_recep, data_receive, multiplexer_4_out, multiplexer_5_out, reg_tx_q, s_rg_rx_p5;

  and AND (AND_out, temp_ok, clk_rx);
  and AND_2 (AND_2_out, tx_finish, inter_tram, wr);
  D_Flip_Flop d_ff_1 (.D(wr), .clk(clock), .Q(d_ff_1_q));  // open: Qn, preset, reset
  // Shift_Register s_rg_rx: pin names not known; wires that end beside it: s_rg_rx_p1, AND_out, clock, Rx_t, s_rg_rx_p5[0], s_rg_rx_p5[1], s_rg_rx_p5[2], s_rg_rx_p5[3], s_rg_rx_p5[4], s_rg_rx_p5[5], s_rg_rx_p5[6], s_rg_rx_p5[7]
  or OR (s_rg_rx_p1, reset, rx_finish);
  Counter #(.width(13), .max('h1458)) counter_1 (
    .clr(OR_2_out), .count(temp_ok), .clk(clock), .carry(clk_rx));  // open: load, up, D, Q
  or OR_2 (OR_2_out, reset, rx_finish);
  D_Flip_Flop d_ff_2 (.D(AND_3_out), .clk(clock), .Q(start));  // open: Qn, preset, reset
  and AND_3 (AND_3_out, wr, inter_tram, tx_finish);
  Register reg_tx (.D(data_in), .en(AND_2_out), .clk(clock), .Q(reg_tx_q), .clr(reset));
  Multiplexer #(.enable("false")) multiplexer_1 (.in0(d_ff_1_q), .in1(1'b0), .out(multiplexer_1_out), .sel(reg_tx_2_q));
  not not_1 (not_1_out, start);
  and AND_4 (AND_4_out, not_1_out, div_clk);
  Register #(.width(1)) reg_tx_2 (.D(not_2_out), .en(AND_5_out), .clk(clock), .Q(reg_tx_2_q), .clr(inter_tram));
  and AND_5 (AND_5_out, not_2_out, multiplexer_1_out);
  // Shift_Register #(.length(10)) s_rg_tx: pin names not known; wires that end beside it: reset, start, AND_4_out, clock, 1'b1, reg_tx_q[0], reg_tx_q[1], reg_tx_q[2], reg_tx_q[3], reg_tx_q[4], reg_tx_q[5], reg_tx_q[6], reg_tx_q[7], 1'b0, 1'b1, s_rg_tx_p16, s_rg_tx_p17, s_rg_tx_p18, s_rg_tx_p19, s_rg_tx_p20, s_rg_tx_p21, s_rg_tx_p22, s_rg_tx_p23, s_rg_tx_p24, s_rg_tx_p25
  not not_2 (not_2_out, reg_tx_2_q);
  not not_3 (not_3_out, temp_ok);
  Register reg_rx (.D(s_rg_rx_p5), .en(receive_done), .clk(clock), .Q(data_receive), .clr(reset));
  and AND_6 (AND_6_out, div_clk, reg_tx_2_q);
  not not_4 (not_4_out, reg_tx_3_q);
  Register #(.width(1)) reg_tx_3 (.D(not_4_out), .en(AND_7_out), .clk(clock), .Q(reg_tx_3_q), .clr(temp_ok));
  and AND_7 (AND_7_out, multiplexer_2_out, not_3_out);
  or OR_3 (OR_3_out, reset, rx_finish);
  Counter #(.width(5), .max('h14)) counter_2 (
    .clr(OR_4_out), .count(AND_6_out), .clk(clock), .carry(inter_tram));  // open: load, up, D, Q
  or OR_4 (OR_4_out, reset, start);
  Multiplexer #(.enable("false")) multiplexer_2 (.in0(Rx), .in1(1'b0), .out(multiplexer_2_out), .sel(reg_tx_3_q));
  Counter #(.width(4), .max('h9)) counter_3 (
    .clr(OR_3_out), .count(clk_rx), .clk(clock), .carry(rx_finish), .Q(counter_3_q));  // open: load, up, D
  and AND_8 (tx_finish, s_rg_tx_p16, s_rg_tx_p17, s_rg_tx_p18, s_rg_tx_p19, s_rg_tx_p20, s_rg_tx_p21, s_rg_tx_p22, s_rg_tx_p23, s_rg_tx_p24, s_rg_tx_p25);
  not not_5 (not_5_out, reg_tx1_q);
  Register #(.width(1)) reg_tx1 (.D(tx_finish), .en(not_5_out), .clk(clock), .Q(reg_tx1_q), .clr(reset));
  Counter #(.width(12), .max('ha2c)) counter_4 (
    .clr(OR_5_out), .count(reg_tx_3_q), .clk(clock), .carry(temp_ok));  // open: load, up, D, Q
  or OR_5 (OR_5_out, reset, rx_finish);
  not not_6 (Tx, multiplexer_3_out);
  Multiplexer #(.enable("false")) multiplexer_3 (
    .in0(1'b1), .in1(s_rg_tx_p25), .out(multiplexer_3_out), .sel(reg_tx1_q));
  not not_7 (Rx_t, Rx);
  Comparator #(.width(4), .mode("unsigned")) comparator_1 (
    .a(counter_3_q), .b(4'b1000), .eq(receive_done));  // open: gt, lt
  and AND_9 (AND_9_out, tx_finish, inter_tram);
  Multiplexer #(.width(8), .enable("false")) multiplexer_4 (
    .in0(8'h10), .in1(8'h20), .out(multiplexer_4_out), .sel(AND_9_out));
  Multiplexer #(.width(8), .enable("false")) multiplexer_5 (
    .in0(8'h10), .in1(8'h20), .out(multiplexer_5_out), .sel(receive_done));
  Multiplexer #(.width(8), .enable("false")) multiplexer_6 (
    .in0(data_out_recep), .in1(multiplexer_4_out), .out(data_out), .sel(address[1]));
  Counter #(.width(13), .max('h1458)) counter_5 (
    .clr(reset), .clk(clock), .carry(div_clk));  // open: load, up, count, D, Q
  Multiplexer #(.width(8), .enable("false")) multiplexer_7 (
    .in0(data_receive), .in1(multiplexer_5_out), .out(data_out_recep), .sel(address[0]));

  // Notes on the sheet:
  //   Partie réception
  //   clock UART RX
  //   Ce compteur est ici pour envoyer une 2ème trame "bidon", pour ralentir le rythme entre 2 trames
  //   Ce compteur est là pour compter les 8 bits à stocker
  //   Ce compteur est là pour les 1.5 bits au début de la réception
  //   Partie transmission
  //   0.5 T à régler
  //   Cette condition est là pour indiquer au cpu que si la réception est terminée
  //   Cette condition est là pour indiquer au cpu si la transmission est terminée
  //   On compte jusqu'à 0x1458 = 5208 pour obtenir les 9600 nécessaires pour le débit UART
  //   clock UART TX
  //   ce tunnel est raccordé au mux de la transmission en haut
endmodule

module system_moteurs (
  input  Rx0,
  input  clock,
  input  reset,
  output cs_pwm0,
  output pwm0_out0,
  output pwm0_out1,
  output cs_pwm1,
  output pwm1_out0,
  output pwm1_out1,
  output b,
  output a,
  output f,
  output g,
  output out0,
  output out1,
  output out2,
  output out3,
  output c,
  output d,
  output e
);

  wire decoder_1_out0, decoder_1_out2, decoder_1_out3, decoder_1_out4, mcpu_read, mcpu_wr;
  wire [7:0] mcpu_address, mcpu_data_out, multiplexer_1_out, uart0_data_out;

  cpu mcpu (
    .clock(clock), .reset(reset), .data_in(multiplexer_1_out), .address(mcpu_address), .wr(mcpu_wr),
    .data_out(mcpu_data_out), .read(mcpu_read));
  Decoder #(.select(4)) decoder_1 (
    .out0(decoder_1_out0), .out2(decoder_1_out2), .out3(decoder_1_out3), .out4(decoder_1_out4),
    .sel(mcpu_address[7:4]), .en(mcpu_wr));  // open: out1, out5, out6, out7, out8, out9, out10, out11, out12, out13, out14, out15
  Multiplexer #(.select(4), .width(8)) multiplexer_1 (
    .in0(uart0_data_out), .out(multiplexer_1_out), .sel(mcpu_address[7:4]), .en(mcpu_read));  // open: in1, in2, in3, in4, in5, in6, in7, in8, in9, in10, in11, in12, in13, in14, in15
  uart uart0 (
    .wr(decoder_1_out0), .data_in(mcpu_data_out), .data_out(uart0_data_out), .address(mcpu_address[3:0]),
    .clock(clock), .reset(reset), .Rx(Rx0));  // open: Tx
  pwm pwm0 (
    .address(mcpu_address[3:0]), .data_in(mcpu_data_out), .clock(clock), .cs(cs_pwm0), .out0(pwm0_out0),
    .out1(pwm0_out1), .reset(reset), .enable(decoder_1_out2));
  pwm pwm1 (
    .address(mcpu_address[3:0]), .data_in(mcpu_data_out), .clock(clock), .cs(cs_pwm1), .out0(pwm1_out0),
    .out1(pwm1_out1), .reset(reset), .enable(decoder_1_out3));
  seg7x4_reg seg_reg (
    .IN0(mcpu_data_out[3:0]), .IN1(mcpu_data_out[7:4]), .enable(decoder_1_out4), .IN2(mcpu_data_out[3:0]),
    .clock(clock), .reset(reset), .IN3(mcpu_data_out[7:4]), .OUT0(out0), .OUT1(out1), .OUT2(out2),
    .OUT3(out3), .b(b), .a(a), .f(f), .g(g), .c(c), .d(d), .e(e), .address(mcpu_address[3:0]));
endmodule
